# Fritzing sketch SENSORE GAS (saved by Fritzing 0.9.3b)
breadboards: 1

parts:
  LED1 = LED - 5mm [color="Red (633nm)" package="5 mm [THT]"]
  LED2 = LED - 5mm [color="Red (633nm)" package="5 mm [THT]"]
  J1 = Piezo Speaker
  LCD1 = LCD screen  # not connected
  Componente1 = Arduino Uno (Rev3)
  LCM1602_IIC1 = LCM1602 IIC [part_number="LCM1602 IIC" chip_label="LCM1602 IIC" package="DIP (Dual Inline) [THT]"]

nets:
  N1: LED1.anode, Componente1.D9_PWM
  GND: LED2.cathode, Componente1.GND, LCM1602_IIC1.GND
  N2: LED2.anode, Componente1.D8
  N3: J1.pin2, Componente1.D4
  N4: Componente1.A4/SDA, LCM1602_IIC1.SDA
  N5: Componente1.A5/SCL, LCM1602_IIC1.SCL
  5V: Componente1.5V, LCM1602_IIC1.VCC

notes:
  VCC | A1 | GND
  SENSORE GAS/FUMO
  MQ-2

custom parts:
  LCM1602 IIC: I2C-Module to use a 1602 or 2004 LCD on with the wire.h libory Serial LCD Modul
